# Fritzing sketch lesson 1 2 and 3 (saved by Fritzing 0.7.4b)
breadboards: 1

parts:
  Nano1 = Arduino Nano v2.3
  R1 = Rotary Potentiometer (Small) [maximum_resistance=100kΩ]
  R2 = Rotary Potentiometer (Small) [maximum_resistance=100kΩ]
  SPKR1 = Loudspeaker

nets:
  N1: Nano1.GND, R1.leg1, R2.leg1, SPKR1.pin1
  N2: Nano1.D9, R2.leg2
  N3: Nano1.A0, R1.wiper
  N4: Nano1.+5V, R1.leg2
  N5: R2.wiper, SPKR1.pin2
